// Logisim project Task4.circ as structural Verilog: 1 circuit, main circuit main
module main (
);

  wire clock_1_out, d_ff_1_q, d_ff_2_q, not_1_out, or_1_out, or_2_out;

  not not_1 (not_1_out, d_ff_1_q);
  or or_1 (or_1_out, not_1_out, d_ff_2_q);
  Clock clock_1 (.out(clock_1_out));
  D_Flip_Flop d_ff_1 (.D(or_1_out), .clk(clock_1_out), .Q(d_ff_1_q));  // open: Qn, preset, reset
  or or_2 (or_2_out, d_ff_2_q, d_ff_1_q);
  D_Flip_Flop d_ff_2 (.D(or_2_out), .clk(clock_1_out), .Q(d_ff_2_q));  // open: Qn, preset, reset
endmodule
